# Fritzing sketch aleksanderkruk_michalsobiech (saved by Fritzing 0.9.3b)
breadboards: 1

parts:
  Raspberry_Pi_1 = Raspberry Pi 3 [part_number=RPI-3-V1.2]
  Part1 = Logic Level Converter
  J1 = Basic Servo
  Part2 = Adafruit VL530X Time of Flight Distance Sensor [part_number="Adafruit #3317"]
  R1 = Resistor [tolerance=±5% resistance=5k package=THT]
  R2 = Resistor [tolerance=±5% resistance=5k package=THT]
  R3 = Resistor [tolerance=±5% resistance=5k package=THT]

nets:
  3V3: Raspberry_Pi_1.3v3, Part1.LV, Part2.VCC, R2.Pin_0, R3.Pin_0
  N1: Raspberry_Pi_1.GPIO2, Part2.SDA, R2.Pin_1
  N2: Raspberry_Pi_1.GPIO3, Part2.SCL, R3.Pin_1
  GND: Raspberry_Pi_1.GND, Part1.GND, J1.gnd, Part2.GND, R1.Pin_0
  N3: Raspberry_Pi_1.GIPO21, Part1.TX2_LV
  5V: Raspberry_Pi_1.5V, Part1.HV, J1.vcc
  N4: Part1.TX2_HV, J1.pulse
  N5: Part2.XSHUT, R1.Pin_1

custom parts:
  Adafruit VL530X Time of Flight Distance Sensor: The VL53L0X is a Time of Flight distance sensor like no other you've used! The sensor contains a very tiny invisible laser source, and a matching sensor. The VL53L0X can detect the "time of flight", or how long the light has taken to bounce back to the sensor. Since it uses a very narrow light source, it is good for determining distance of only the surface directly in front of it. Unlike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
